# Fritzing sketch Web_Server_LED (saved by Fritzing 0.9.3b)
breadboards: 1

parts:
  U1 = NodeMCU V1.0
  R1 = Resistor [tolerance=±5% resistance=220 package=THT]
  LED1 = LED - 5mm [color="Red (633nm)" package="5 mm [THT]"]

nets:
  N1: U1.D1, R1.Pin_0
  N2: U1.GND#13, LED1.cathode
  N3: R1.Pin_1, LED1.anode

custom parts:
  NodeMCU V1.0: ESP8266 based NodeMCU V1.0
