# Fritzing sketch RFID_GirisSistemi (saved by Fritzing 0.9.3b)
breadboards: 1

parts:
  Part2 = RFID-RC522-v2
  R1 = Resistor [tolerance=±5% resistance=330 package=THT]
  R2 = Resistor [tolerance=±5% resistance=330 package=THT]
  LED1 = LED - 5mm [color="Red (633nm)" package="5 mm [THT]"]
  LED2 = LED - 5mm [color="Green (555nm)" package="5 mm [THT]"]
  U1 = NodeMCU V1.0
  J1 = Piezo Speaker

nets:
  N1: Part2.SDA, U1.D4
  N2: Part2.SCK, U1.D5
  N3: Part2.MOSI, U1.D7
  N4: Part2.MISO, U1.D6
  N5: Part2.GND, LED1.cathode, LED2.cathode, U1.GND#13, J1.pin1
  N6: Part2.RST, U1.D3
  N7: Part2.3_3V, U1.3V3#14
  N8: R1.Pin_0, LED1.anode
  N9: R1.Pin_1, U1.D2
  N10: R2.Pin_0, LED2.anode
  N11: R2.Pin_1, U1.D1
  N12: U1.D8, J1.pin2

notes:
  NodeMCU RC522 RFID
  --------------------------------------------------
  D4 (Gri) SDA (SS)
  D5 (Mavi) SCK
  D6 (Beyaz) MISO
  D7 (Turuncu) MOSI
  NodeMCU RC522 RFID
  --------------------------------------------------
  D3 (Sarı) RST
  3V (Kırmızı) 3.3V
  GND (Siyah) GND

custom parts:
  RFID-RC522-v2: A simple China made RFID-RC522 Reader; do check the pin labels, as this is a MFRC522 based clone.
  NodeMCU V1.0: ESP8266 based NodeMCU V1.0
